# Fritzing sketch weather_clock (saved by Fritzing 0.9.2b)
breadboards: 1

parts:
  Part1 = Photon
  VCC1 = 4 x AAA Battery Mount
  J1 = Basic Servo

nets:
  GND: Part1.GND, VCC1.-, J1.gnd
  N1: Part1.VIN, VCC1.+
  N2: Part1.D0, J1.pulse
  3V3: Part1.3V3, J1.vcc
